// Digital circuit FlagsRegisterFileProiectFic.dig as structural Verilog
module FlagsRegisterFileProiectFic (
  input  zero,
  input  C,
  input  negative,
  input  carry,
  input  overflow,
  output ZERO_2,
  output NEG,
  output CARRY_2,
  output OVERFLOW_2
);

  Register u_ZERO (.D(zero), .C(C), .en(1'b1), .Q(ZERO_2));
  Register u_NEG (.D(negative), .C(C), .en(1'b1), .Q(NEG));
  Register u_CARRY (.D(carry), .C(C), .en(1'b1), .Q(CARRY_2));
  Register u_OVERFLOW (.D(overflow), .C(C), .en(1'b1), .Q(OVERFLOW_2));
endmodule
