// Digital circuit ProcesorProiectFIC.dig as structural Verilog
// The program counter.
// Here the current program counter is stored.
// The various inputs can be used to influence how the 
// program counter is modified if a clock signal happens.
// {{de Der Programmzähler. 
// Hier wird der aktuelle Programmzähler gespeichert. 
// Über die verschiedenen Eingänge kann beeinflußt 
// werden, auf welche Weise der Programmzähler mit 
// dem Takt weiter geschaltet wird.}}
module ProcesorProiectFIC (
  input  clk,
  input  [15:0] in_2,
  input  in_3,
  input  in_4,
  input  in_5,
  input  in_6,
  input  in_7
);

  wire aluproiectfic_1_carry, aluproiectfic_1_neg, aluproiectfic_1_overflow, aluproiectfic_1_zero, Carry,
       cmpImm1, cmpImm2, controlunit_1_writeregisterfile, delay_1_out, instructiondecoderproiectfic_1_malu,
       instructiondecoderproiectfic_1_mload, instructiondecoderproiectfic_1_mmov,
       instructiondecoderproiectfic_1_mstore, jmpOp, loadOp, M, multiplexer_6_out, Neg, not_1_out, not_2_out,
       Overflow, reset_1_out, retOp, selPC, stackOp, usageALU, zero, ZeroFlag;
  wire [1:0] instructiondecoderproiectfic_1_mcmp, instructiondecoderproiectfic_1_rd,
       instructiondecoderproiectfic_1_rs1, instructiondecoderproiectfic_1_rs2;
  wire [4:0] instructiondecoderproiectfic_1_opcode;
  wire [10:0] instructiondecoderproiectfic_1_sgnext, instructiondecoderproiectfic_1_signext2;
  wire [15:0] aluproiectfic_1_y, DM_d, IM_d, multiplexer_1_out, multiplexer_2_out, multiplexer_3_out,
       multiplexer_4_out, multiplexer_5_out, multiplexer_7_out, multiplexer_8_out, multiplexer_9_out,
       multiplexer_10_out, multiplexer_11_out, multiplexer_12_out, multiplexer_13_out, multiplexer_14_out,
       multiplexer_15_out, one, PC_plus_ALU_s, PC_q, PCval, registerfileproiectfic_1_p7,
       registerfileproiectfic_1_p8, registerfileproiectfic_1_p9, signextendunit_1_immediate1,
       signextendunit_1_immediate2, SP_1_s, SP_plus_1_s, SP_q;

  Multiplexer #(.Bits(16)) multiplexer_1 (.sel(selPC), .in_0(PCval), .in_1(PC_plus_ALU_s), .out(multiplexer_1_out));
  Multiplexer #(.Bits(16)) multiplexer_2 (
    .sel(in_4), .in_0(multiplexer_1_out), .in_1({16{1'b0}}), .out(multiplexer_2_out));
  Register #(.Bits(16), .isProgramCounter("true")) PC (.D(multiplexer_2_out), .C(clk), .en(reset_1_out), .Q(PC_q));
  Reset reset_1 (.out(reset_1_out));
  Add #(.Bits(16)) PC_plus_1 (.a(PC_q), .b(one), .c_i(zero), .s(PCval));  // open: c_o
  not not_1 (not_1_out, in_3);
  RAMDualPort #(.AddrBits(16), .isProgramMemory("true"), .Bits(16)) IM (
    .A(PC_q), .Din(in_2), .str(in_3), .C(clk), .ld(not_1_out), .D(IM_d));
  InstructionDecoderProiectFIC instructiondecoderproiectfic_1 (
    .Instruction(IM_d), .RD(instructiondecoderproiectfic_1_rd),
    .SgnExt(instructiondecoderproiectfic_1_sgnext), .RS2(instructiondecoderproiectfic_1_rs2),
    .RS1(instructiondecoderproiectfic_1_rs1), .SignExt2(instructiondecoderproiectfic_1_signext2),
    .MLoad(instructiondecoderproiectfic_1_mload), .MALU(instructiondecoderproiectfic_1_malu),
    .MStore(instructiondecoderproiectfic_1_mstore), .MMov(instructiondecoderproiectfic_1_mmov),
    .MCmp(instructiondecoderproiectfic_1_mcmp), .OpCode(instructiondecoderproiectfic_1_opcode));
  Add #(.Bits(16)) PC_plus_ALU (.a({16{1'b0}}), .b(aluproiectfic_1_y), .c_i(zero), .s(PC_plus_ALU_s));  // open: c_o
  ControlUnit controlunit_1 (
    .OpCode(instructiondecoderproiectfic_1_opcode), .MCmp(instructiondecoderproiectfic_1_mcmp),
    .MLoad(instructiondecoderproiectfic_1_mload), .MStore(instructiondecoderproiectfic_1_mstore),
    .MALU(instructiondecoderproiectfic_1_malu), .MMov(instructiondecoderproiectfic_1_mmov),
    .ZERO_2(ZeroFlag), .NEG(Neg), .CARRY(Carry), .OVERFLOW(Overflow), .usageALU(usageALU), .M(M),
    .zero(zero), .one(one), .loadOp(loadOp), .cmpImmediate1(cmpImm1), .retOp(retOp), .jmpOp(jmpOp),
    .stackOp(stackOp), .selPC(selPC), .cmpImmediate2(cmpImm2),
    .writeRegisterFile(controlunit_1_writeregisterfile));
  SignExtendUnit signextendunit_1 (
    .SgnExt1(instructiondecoderproiectfic_1_sgnext), .SgnExt2(instructiondecoderproiectfic_1_signext2),
    .Immediate1(signextendunit_1_immediate1), .Immediate2(signextendunit_1_immediate2));
  Delay delay_1 (.in(clk), .out(delay_1_out));
  Multiplexer #(.Bits(16)) multiplexer_3 (
    .sel(usageALU), .in_0(signextendunit_1_immediate1), .in_1(aluproiectfic_1_y), .out(multiplexer_3_out));
  Multiplexer #(.Bits(16)) multiplexer_4 (.sel(loadOp), .in_0(multiplexer_3_out), .in_1(DM_d), .out(multiplexer_4_out));
  // RegisterFileProiectFIC registerfileproiectfic_1: pin names not known; wires that end beside it: multiplexer_4_out, delay_1_out, instructiondecoderproiectfic_1_rs1, instructiondecoderproiectfic_1_rd, instructiondecoderproiectfic_1_rs2, controlunit_1_writeregisterfile, registerfileproiectfic_1_p7, registerfileproiectfic_1_p8, registerfileproiectfic_1_p9
  Multiplexer #(.Bits(16)) multiplexer_5 (
    .sel(multiplexer_6_out), .in_0(registerfileproiectfic_1_p8), .in_1(registerfileproiectfic_1_p9),
    .out(multiplexer_5_out));
  Multiplexer multiplexer_6 (
    .sel(usageALU), .in_0(instructiondecoderproiectfic_1_rs2[0]), .in_1(usageALU), .out(multiplexer_6_out));
  Multiplexer #(.Bits(16)) multiplexer_7 (
    .sel(cmpImm1), .in_0(registerfileproiectfic_1_p7), .in_1(signextendunit_1_immediate1),
    .out(multiplexer_7_out));
  Multiplexer #(.Bits(16)) multiplexer_8 (
    .sel(M), .in_0(multiplexer_5_out), .in_1(signextendunit_1_immediate1), .out(multiplexer_8_out));
  Multiplexer #(.Bits(16)) multiplexer_9 (
    .sel(cmpImm2), .in_0(multiplexer_8_out), .in_1(signextendunit_1_immediate2), .out(multiplexer_9_out));
  ALUProiectFIC aluproiectfic_1 (
    .A(multiplexer_7_out), .B(multiplexer_9_out), .Op(instructiondecoderproiectfic_1_opcode),
    .Y(aluproiectfic_1_y), .Zero(aluproiectfic_1_zero), .Neg(aluproiectfic_1_neg),
    .Carry(aluproiectfic_1_carry), .UsgALU(usageALU), .Overflow(aluproiectfic_1_overflow));  // open: UsgALUC
  // FlagsRegisterFileProiectFic flagsregisterfileproiectfic_1: pin names not known; wires that end beside it: aluproiectfic_1_zero, clk, aluproiectfic_1_neg, aluproiectfic_1_carry, aluproiectfic_1_overflow, ZeroFlag, Neg, Carry, Overflow
  Multiplexer #(.Bits(16)) multiplexer_10 (
    .sel(jmpOp), .in_0(multiplexer_9_out), .in_1(PCval), .out(multiplexer_10_out));
  Multiplexer #(.Bits(16)) multiplexer_11 (
    .sel(stackOp), .in_0(aluproiectfic_1_y), .in_1(multiplexer_14_out), .out(multiplexer_11_out));
  not not_2 (not_2_out, in_5);
  RAMDualPort #(.AddrBits(16), .isProgramMemory("true"), .Bits(16)) DM (
    .A(multiplexer_11_out), .Din(multiplexer_10_out), .str(in_5), .C(clk), .ld(not_2_out), .D(DM_d));
  Multiplexer #(.Bits(16)) multiplexer_12 (.sel(retOp), .in_0(SP_1_s), .in_1(SP_plus_1_s), .out(multiplexer_12_out));
  Multiplexer #(.Bits(16)) multiplexer_13 (
    .sel(stackOp), .in_0(SP_q), .in_1(multiplexer_12_out), .out(multiplexer_13_out));
  Multiplexer #(.Bits(16)) multiplexer_14 (
    .sel(retOp), .in_0(SP_q), .in_1(multiplexer_15_out), .out(multiplexer_14_out));
  Multiplexer #(.Bits(16)) multiplexer_15 (
    .sel(in_7), .in_0(multiplexer_13_out), .in_1({16{1'b1}}), .out(multiplexer_15_out));
  Sub #(.Bits(16)) SP_1 (.a(SP_q), .b(16'h1), .c_i(1'b0), .s(SP_1_s));  // open: c_o
  Register #(.Bits(16)) SP (.D(multiplexer_15_out), .C(clk), .en(in_6), .Q(SP_q));
  Add #(.Bits(16)) SP_plus_1 (.a(SP_q), .b(16'h1), .c_i(1'b0), .s(SP_plus_1_s));  // open: c_o

  // Other names for the same wires on the sheet: enSP = in_6; rstPC = in_4; startSP = in_7; strDM = in_5;
  //   strIM = in_3
endmodule
